// Logisim project Ctl_Conditional.circ as structural Verilog: 1 circuit, main circuit Conditional
module Conditional (
  input  Enable,
  input  [15:0] Instruction,
  input  Z,
  input  C,
  input  N,
  input  V,
  output [10:0] Offset,
  output Verified
);

  wire and_1_out, and_2_out, and_3_out, and_4_out, and_5_out, and_6_out, and_7_out, and_8_out, and_9_out,
       and_10_out, and_11_out, and_12_out, and_13_out, and_14_out, and_15_out, and_16_out, and_17_out,
       and_18_out, and_19_out, and_20_out, and_21_out, not_1_out, not_2_out, not_3_out, not_4_out, not_5_out,
       not_6_out, not_7_out, not_8_out, not_9_out, not_10_out, not_11_out, not_12_out, not_13_out,
       not_14_out, not_15_out, not_16_out, not_17_out, not_18_out, not_19_out, not_20_out, not_21_out,
       not_22_out, not_23_out, not_24_out, not_25_out, not_26_out, not_27_out, not_28_out, not_29_out,
       not_30_out, not_31_out, not_32_out, not_33_out, not_34_out, not_35_out, not_36_out, not_37_out,
       not_38_out, not_39_out, not_40_out, or_1_out, or_2_out, or_3_out, xnor_1_out, xnor_2_out, xor_1_out,
       xor_2_out;
  wire [10:0] bit_extender_1_out, multiplexer_1_out, multiplexer_2_out;

  not not_1 (not_1_out, Instruction[9]);
  not not_2 (not_2_out, Instruction[10]);
  not not_3 (not_3_out, Instruction[11]);
  not not_4 (not_4_out, Instruction[9]);
  not not_5 (not_5_out, Instruction[10]);
  not not_6 (not_6_out, Instruction[11]);
  not not_7 (not_7_out, Z);
  not not_8 (not_8_out, Instruction[10]);
  not not_9 (not_9_out, Instruction[11]);
  not not_10 (not_10_out, Instruction[10]);
  not not_11 (not_11_out, Instruction[11]);
  not not_12 (not_12_out, C);
  not not_13 (not_13_out, Instruction[9]);
  not not_14 (not_14_out, Instruction[11]);
  not not_15 (not_15_out, Instruction[9]);
  not not_16 (not_16_out, Instruction[11]);
  not not_17 (not_17_out, N);
  not not_18 (not_18_out, Instruction[11]);
  not not_19 (not_19_out, Instruction[11]);
  not not_20 (not_20_out, V);
  not not_21 (not_21_out, Instruction[9]);
  not not_22 (not_22_out, Instruction[10]);
  not not_23 (not_23_out, Z);
  and and_1 (and_1_out, not_23_out, C);
  not not_24 (not_24_out, Instruction[9]);
  not not_25 (not_25_out, Instruction[10]);
  or or_1 (or_1_out, Z, not_26_out);
  not not_26 (not_26_out, C);
  not not_27 (not_27_out, Instruction[10]);
  xnor xnor_1 (xnor_1_out, N, V);
  not not_28 (not_28_out, Instruction[10]);
  xor xor_1 (xor_1_out, N, V);
  not not_29 (not_29_out, Instruction[9]);
  not not_30 (not_30_out, Z);
  and and_2 (and_2_out, not_30_out, xnor_2_out);
  xnor xnor_2 (xnor_2_out, N, V);
  not not_31 (not_31_out, Instruction[9]);
  xor xor_2 (xor_2_out, N, V);
  not not_32 (not_32_out, Instruction[8]);
  and and_3 (and_3_out, not_32_out, not_1_out, not_2_out, not_3_out, Z);
  and and_4 (and_4_out, Instruction[8], not_4_out, not_5_out, not_6_out, not_7_out);
  not not_33 (not_33_out, Instruction[8]);
  and and_5 (and_5_out, not_33_out, Instruction[9], not_8_out, not_9_out, C);
  and and_6 (and_6_out, Instruction[8], Instruction[9], not_10_out, not_11_out, not_12_out);
  not not_34 (not_34_out, Instruction[8]);
  and and_7 (and_7_out, not_34_out, not_13_out, Instruction[10], not_14_out, N);
  and and_8 (and_8_out, Instruction[8], not_15_out, Instruction[10], not_16_out, not_17_out);
  not not_35 (not_35_out, Instruction[8]);
  and and_9 (and_9_out, not_35_out, Instruction[9], Instruction[10], not_18_out, V);
  and and_10 (and_10_out, Instruction[8], Instruction[9], Instruction[10], not_19_out, not_20_out);
  not not_36 (not_36_out, Instruction[8]);
  and and_11 (and_11_out, not_36_out, not_21_out, not_22_out, Instruction[11], and_1_out);
  and and_12 (and_12_out, Instruction[8], not_24_out, not_25_out, Instruction[11], or_1_out);
  not not_37 (not_37_out, Instruction[8]);
  and and_13 (and_13_out, not_37_out, Instruction[9], not_27_out, Instruction[11], xnor_1_out);
  and and_14 (and_14_out, Instruction[8], Instruction[9], not_28_out, Instruction[11], xor_1_out);
  not not_38 (not_38_out, Instruction[8]);
  and and_15 (and_15_out, not_38_out, not_29_out, Instruction[10], Instruction[11], and_2_out);
  and and_16 (and_16_out, Instruction[8], not_31_out, Instruction[10], Instruction[11], or_2_out);
  or or_2 (or_2_out, Z, xor_2_out);
  not not_39 (not_39_out, Instruction[8]);
  and and_17 (and_17_out, not_39_out, Instruction[9], Instruction[10], Instruction[11]);
  and and_18 (and_18_out, Instruction[8], Instruction[9], Instruction[10], Instruction[11]);
  not not_40 (not_40_out, and_18_out);
  and and_19 (and_19_out, not_40_out, Enable);
  or or_3 (or_3_out, and_3_out, and_4_out, and_5_out, and_6_out, and_7_out, and_8_out, and_9_out, and_10_out, and_11_out, and_12_out, and_13_out, and_14_out, and_15_out, and_16_out, and_17_out);
  assign bit_extender_1_out = {{3{Instruction[7]}}, Instruction[7:0]};  // Bit_Extender bit_extender_1
  and and_20 (and_20_out, Enable, Instruction[13]);
  or or_4 (Verified, and_20_out, and_21_out);
  and and_21 (and_21_out, or_3_out, and_19_out);
  Multiplexer #(.enable("false"), .width(11)) multiplexer_1 (
    .in0(bit_extender_1_out), .in1(Instruction[10:0]), .out(multiplexer_1_out), .sel(Instruction[13]));
  Multiplexer #(.enable("false"), .width(11)) multiplexer_2 (
    .in0({11{1'b0}}), .in1(multiplexer_1_out), .out(multiplexer_2_out), .sel(Enable));
  Multiplexer #(.enable("false"), .width(11)) multiplexer_3 (
    .in0({11{1'b0}}), .in1(multiplexer_2_out), .out(Offset), .sel(Verified));

  // Other names for the same wires on the sheet: IMM8[7:0] = Instruction[7:0]; b8 = Instruction[8];
  //   b9 = Instruction[9]; b10 = Instruction[10]; b11 = Instruction[11]; b13 = Instruction[13]
endmodule
