// Logisim project Ctl_Data_Processing.circ as structural Verilog: 1 circuit, main circuit Data_Processing
module Data_Processing (
  input  [15:0] Instruction,
  input  [3:0] in_2,
  input  Enable,
  input  [3:0] in_4,
  input  [3:0] in_5,
  output [2:0] Rd,
  output [2:0] Rn,
  output [2:0] Rm,
  output [3:0] ALU_Opcode,
  output [3:0] Flags_Update_Mask
);

  wire decoder_1_out0, decoder_1_out1, decoder_1_out2, decoder_1_out3, decoder_1_out4, decoder_1_out5,
       decoder_1_out6, decoder_1_out7, decoder_1_out8, decoder_1_out9, decoder_1_out10, decoder_1_out11,
       decoder_1_out12, decoder_1_out13, decoder_1_out14, decoder_1_out15, or_1_out, or_2_out;
  wire [3:0] and_2_out, and_3_out, and_4_out, bit_extender_2_out, bit_extender_3_out, bit_extender_4_out;
  wire [15:0] bit_extender_1_out;
  wire [15:10] and_1_out;

  assign bit_extender_1_out = {{15{Enable}}, Enable};  // Bit_Extender bit_extender_1
  assign {and_1_out, ALU_Opcode, Rm, Rd} = Instruction & bit_extender_1_out;  // AND_Gate and_1, 16 bits wide
  Decoder #(.select(4)) decoder_1 (
    .out0(decoder_1_out0), .out1(decoder_1_out1), .out2(decoder_1_out2), .out3(decoder_1_out3),
    .out4(decoder_1_out4), .out5(decoder_1_out5), .out6(decoder_1_out6), .out7(decoder_1_out7),
    .out8(decoder_1_out8), .out9(decoder_1_out9), .out10(decoder_1_out10), .out11(decoder_1_out11),
    .out12(decoder_1_out12), .out13(decoder_1_out13), .out14(decoder_1_out14), .out15(decoder_1_out15),
    .sel(ALU_Opcode), .en(Enable));
  or or_1 (or_1_out, decoder_1_out0, decoder_1_out1, decoder_1_out2, decoder_1_out3, decoder_1_out4, decoder_1_out7, decoder_1_out8, decoder_1_out12, decoder_1_out14, decoder_1_out15);
  or or_2 (or_2_out, decoder_1_out5, decoder_1_out6, decoder_1_out9, decoder_1_out10, decoder_1_out11);
  assign bit_extender_2_out = {{3{or_1_out}}, or_1_out};  // Bit_Extender bit_extender_2
  assign bit_extender_3_out = {{3{or_2_out}}, or_2_out};  // Bit_Extender bit_extender_3
  assign bit_extender_4_out = {{3{decoder_1_out13}}, decoder_1_out13};  // Bit_Extender bit_extender_4
  assign and_2_out = bit_extender_2_out & in_2;  // AND_Gate and_2, 4 bits wide
  assign and_3_out = bit_extender_3_out & in_4;  // AND_Gate and_3, 4 bits wide
  assign and_4_out = bit_extender_4_out & in_5;  // AND_Gate and_4, 4 bits wide
  assign Flags_Update_Mask = and_2_out | and_3_out | and_4_out;  // OR_Gate or_3, 4 bits wide

  assign Rn = Rd;

  // Notes on the sheet:
  //   Note 2: RSB instruction has Rn as 1st operand.
  //   MUL instruction has Rn as 1st operand and Rdm as 2nd operand
  //   For simplification purposes, Rm is used for 1st operand both here and in the ALU.
  //   Note: instructions that does not save the result will still have the second operand as the destination register, the ALU will copy the second register to the destination register
endmodule
