// Logisim project Ctl_Load_Store.circ as structural Verilog: 1 circuit, main circuit Load_Store
module Load_Store (
  input  [15:0] Instruction,
  input  Reset,
  input  Enable,
  input  [31:0] Stack_Pointer,
  input  Clk,
  output [31:0] RAM_Addr,
  output Store,
  output Load,
  output PC_Hold,
  output [2:0] Rmd
);

  wire and_2_out, d_ff_1_q, d_ff_1_qn, not_1_out, not_2_out, not_3_out;
  wire [31:0] bit_extender_1_out;

  assign bit_extender_1_out = {{24{Instruction[7]}}, Instruction[7:0]};  // Bit_Extender bit_extender_1
  not not_1 (not_1_out, Instruction[11]);
  not not_2 (not_2_out, d_ff_1_q);
  Multiplexer #(.enable("false"), .width(3)) multiplexer_1 (
    .in0(3'b000), .in1(Instruction[10:8]), .out(Rmd), .sel(Enable));
  and and_1 (Store, Enable, not_1_out);
  and and_2 (and_2_out, not_2_out, Enable);
  Adder #(.width(32)) adder_1 (.a(bit_extender_1_out), .b(Stack_Pointer), .out(RAM_Addr));  // open: cin, cout
  D_Flip_Flop d_ff_1 (.D(and_2_out), .clk(Clk), .Q(d_ff_1_q), .Qn(d_ff_1_qn), .reset(Reset));  // open: preset
  not not_3 (not_3_out, d_ff_1_qn);
  and and_3 (Load, Enable, Instruction[11], not_3_out);
  and and_4 (PC_Hold, d_ff_1_q, Enable);

  // Other names for the same wires on the sheet: RMD_t[2:0] = Instruction[10:8]

  // Notes on the sheet:
  //   Instruction: pull=down
  //   Delay load and hold PC for 1 cycle for the RAM to send out requested data 
endmodule
